# Fritzing sketch ESP (saved by Fritzing 0.9.2b)
breadboards: 1

parts:
  U1 = NodeMCU V1.0
  LED1 = RGB LED (com. cathode, rbg) [package="5 mm [THT]"]
  LED2 = RGB LED (com. cathode, rbg) [package="5 mm [THT]"]
  R1 = Resistor [tolerance=±5% resistance=200 package=THT]  # not connected
  R2 = Resistor [tolerance=±5% resistance=200 package=THT]
  R3 = Resistor [tolerance=±5% resistance=200 package=THT]

nets:
  N1: U1.GND, LED1.common_cathode, LED2.common_cathode
  N2: LED1.blue_anode, R2.Pin_1
  N3: LED1.green_anode, R3.Pin_1

custom parts:
  NodeMCU V1.0: ESP8266 based NodeMCU
